// Digital circuit CPU.dig as structural Verilog
module CPU (
  input  CLK_RAW,
  input  in_12,
  input  in_20,
  input  in_21,
  input  in_24,
  input  in_25,
  output [31:0] x8_s0_fp,
  output [31:0] x9_s1,
  output [31:0] x10_a0,
  output [31:0] PC,
  output [31:0] ADDR,
  output [31:0] Instr,
  output [7:0] Dout,
  output [4:0] Step,
  output [7:0] Substep,
  output [7:0] Dval,
  output [15:0] out_13,
  output [15:0] out_14,
  output out_15,
  output [31:0] out_16,
  output BUS_CLK,
  output [31:0] out_18,
  output [31:0] out_19,
  output [31:0] out_22,
  output [11:0] CSR_Address,
  output [31:0] x11_a1,
  output [31:0] x12_a2,
  output [31:0] x13_a3,
  output [31:0] x14_a4,
  output [31:0] x15_a5,
  output [31:0] x1_ra,
  output [31:0] x2_sp,
  output [31:0] x3_gp,
  output [31:0] x4_tp,
  output [31:0] x5_t0,
  output [31:0] x6_t1,
  output [31:0] x7_t2,
  output [7:0] out_38,
  output [5:0] out_39
);

  wire ADDR_CLK, ADDR_IN, ADDR_LATCH, ALU_A, ALU_B, ALU_FLAG_LATCH, ALU_N, alu_shift_step_1_loadlen_sh,
       alu_shift_step_1_noutput_sh, alu_shift_step_1_reset_sh, and_2_out, B_INSTR, B_RUN, B_STEP, B_STOP,
       B_SUBSTEP, BUS_EN, CLK, clock_1_lastsubstep, clock_driver_1_running, Const1, Const31, CSR_OUT,
       d_ff_1_q, d_ff_2_q, ImmB, ImmCSR, ImmI, ImmJ, ImmS, ImmU, IRQ_OP, IRQ_OP_SnP, LASTSTEP, MEM_IN,
       MEM_OUT, MEPC_OUT, MTVEC_OUT, multiplexer_6_out, nADDR_PE, nALU_RESET, nand_1_out, nCLK, nMEM_OE,
       nMEM_WE, nOPDONE, not_1_out, nPC_CNT_PE, nREG_IN_EN, nRESET, nS_EXT, nSTEPDONE, OP_IN, OP_IN_MUX,
       OP_LATCH, opcode_1_p15, opcode_1_p16, opcode_1_p23, PC_IN, PC_IN_LATCH, PC_OUT, PC_OUT_SnP, REG_IN,
       RESET, ROM_SEL, RS1;
  wire [1:0] ALU_A_MUX, LEN, REG_IN_MUX;
  wire [2:0] ALU_B_MUX, ALU_OP;
  wire [3:0] RSD;
  wire [7:0] demultiplexer_1_out_0, demultiplexer_1_out_8, ROM_DATA;
  wire [15:0] ROM_ADDR;
  wire [31:12] MicroCode_d;

  DebugShift32 debugshift32_1 (.CLK(BUS_CLK), .D(REG_IN), .nEN(demultiplexer_1_out_0[1]), .Val(x1_ra));
  DebugShift32 debugshift32_2 (.CLK(BUS_CLK), .D(REG_IN), .nEN(demultiplexer_1_out_0[2]), .Val(x2_sp));
  DebugShift32 debugshift32_3 (.CLK(BUS_CLK), .D(REG_IN), .nEN(demultiplexer_1_out_0[3]), .Val(x3_gp));
  DebugShift32 debugshift32_4 (.CLK(BUS_CLK), .D(REG_IN), .nEN(demultiplexer_1_out_0[4]), .Val(x4_tp));
  DebugShift32 debugshift32_5 (.CLK(BUS_CLK), .D(REG_IN), .nEN(demultiplexer_1_out_0[5]), .Val(x5_t0));
  DebugShift32 debugshift32_6 (.CLK(BUS_CLK), .D(REG_IN), .nEN(demultiplexer_1_out_0[6]), .Val(x6_t1));
  DebugShift32 debugshift32_7 (.CLK(BUS_CLK), .D(REG_IN), .nEN(demultiplexer_1_out_0[7]), .Val(x7_t2));
  Button #(.activeLow("true")) Stop (.out(B_STOP));
  Button #(.activeLow("true")) Run (.out(B_RUN));
  Button #(.activeLow("true")) One_Instruction (.out(B_INSTR));
  Button #(.activeLow("true")) One_Step (.out(B_STEP));
  Button #(.activeLow("true")) One_Substep (.out(B_SUBSTEP));
  Demultiplexer #(.Selector_Bits(4), .Default(1)) demultiplexer_1 (
    .sel(RSD), .in(nREG_IN_EN), .out_0(demultiplexer_1_out_0[0]), .out_1(demultiplexer_1_out_0[1]),
    .out_2(demultiplexer_1_out_0[2]), .out_3(demultiplexer_1_out_0[3]), .out_4(demultiplexer_1_out_0[4]),
    .out_5(demultiplexer_1_out_0[5]), .out_6(demultiplexer_1_out_0[6]), .out_7(demultiplexer_1_out_0[7]),
    .out_8(demultiplexer_1_out_8[0]), .out_9(demultiplexer_1_out_8[1]), .out_10(demultiplexer_1_out_8[2]),
    .out_11(demultiplexer_1_out_8[3]), .out_12(demultiplexer_1_out_8[4]), .out_13(demultiplexer_1_out_8[5]),
    .out_14(demultiplexer_1_out_8[6]), .out_15(demultiplexer_1_out_8[7]));
  DebugShift32 debugshift32_8 (.CLK(BUS_CLK), .D(REG_IN), .nEN(demultiplexer_1_out_8[0]), .Val(x8_s0_fp));
  DebugShift32 debugshift32_9 (.CLK(BUS_CLK), .D(REG_IN), .nEN(demultiplexer_1_out_8[1]), .Val(x9_s1));
  DebugShift32 debugshift32_10 (.CLK(BUS_CLK), .D(REG_IN), .nEN(demultiplexer_1_out_8[2]), .Val(x10_a0));
  DebugShift32 debugshift32_11 (.CLK(BUS_CLK), .D(REG_IN), .nEN(demultiplexer_1_out_8[3]), .Val(x11_a1));
  DebugShift32 debugshift32_12 (.CLK(BUS_CLK), .D(REG_IN), .nEN(demultiplexer_1_out_8[4]), .Val(x12_a2));
  DebugShift32 debugshift32_13 (.CLK(BUS_CLK), .D(REG_IN), .nEN(demultiplexer_1_out_8[5]), .Val(x13_a3));
  DebugShift32 debugshift32_14 (.CLK(BUS_CLK), .D(REG_IN), .nEN(demultiplexer_1_out_8[6]), .Val(x14_a4));
  DebugShift32 debugshift32_15 (.CLK(BUS_CLK), .D(REG_IN), .nEN(demultiplexer_1_out_8[7]), .Val(x15_a5));
  D_FF d_ff_1 (.D(OP_LATCH), .C(CLK), .Q(d_ff_1_q));  // open: nQ
  Reset reset_1 (.out(nRESET));
  Reset #(.invertOutput("false")) reset_2 (.out(RESET));
  // PC pc_1: pin names not known; wires that end beside it: CLK, BUS_CLK, PC_IN, PC_IN_LATCH, LASTSTEP, PC_OUT_SnP, nPC_CNT_PE, OP_LATCH, nRESET, PC_OUT, PC
  // OpCode opcode_1: pin names not known; wires that end beside it: BUS_CLK, OP_IN, OP_LATCH, d_ff_1_q, BUS_EN, nRESET, ImmI, ImmS, ImmB, ImmU, ImmJ, Const1, Const31, ImmCSR, opcode_1_p15, opcode_1_p16, RSD, out_13[9:5], out_13[12:10], out_13[13], nS_EXT, out_13[15], opcode_1_p23, Instr, out_14
  nand nand_1 (nand_1_out, PC_OUT_SnP, OP_IN_MUX);
  Clock_driver clock_driver_1 (
    .CLK_RAW(CLK_RAW), .Stop(B_STOP), .Run(B_RUN), .One_Instruction(B_INSTR), .One_Step(B_STEP),
    .One_Substep(B_SUBSTEP), .nSTEPDONE(nSTEPDONE), .nOPDONE(nOPDONE), .nRESET(nRESET), .CLK(CLK),
    .nCLK(nCLK), .Running(clock_driver_1_running));
  and and_1 (BUS_CLK, CLK, BUS_EN);
  not not_1 (not_1_out, clock_driver_1_running);
  // Mem mem_1: pin names not known; wires that end beside it: CLK, BUS_CLK, MEM_IN, ADDR_IN, ADDR_LATCH, ADDR_CLK, nADDR_PE, nMEM_OE, nMEM_WE, nRESET, ROM_DATA, nS_EXT, MEM_OUT, ADDR, Dout, Dval, ROM_ADDR, ROM_SEL, out_38
  LED led_1 (.in(clock_driver_1_running));
  LED led_2 (.in(not_1_out));
  // Register_bank register_bank_1: pin names not known; wires that end beside it: BUS_CLK, REG_IN, nREG_IN_EN, opcode_1_p15, opcode_1_p16, RSD, RESET, RS1, MEM_IN
  Interrupt_Controller interrupt_controller_1 (
    .BUS_CLK(BUS_CLK), .MEPC_IN(PC_OUT), .nMEPC_IN_EN(nand_1_out), .IRQ_OP_SnP(IRQ_OP_SnP),
    .MTVEC_SnP(in_21), .LASTSTEP(LASTSTEP), .IRQ(in_20), .OP_LATCH(OP_LATCH), .RESET(RESET), .nRESET(nRESET),
    .MEPC_OUT(MEPC_OUT), .IRQ_OP(IRQ_OP), .MTVEC_OUT(MTVEC_OUT), .IRQ_OP_FETCH(OP_IN_MUX), .MEPC(out_22));
  Clock clock_1 (
    .CLK(CLK), .nCLK(nCLK), .LEN(LEN), .LASTSTEP(LASTSTEP), .nRESET(nRESET), .STEP(out_13[4:0]),
    .LASTSUBSTEP(clock_1_lastsubstep), .nSTEPDONE(nSTEPDONE), .SUBSTEP(Substep), .nOPDONE(nOPDONE));
  Multiplexer #(.Selector_Bits(3)) multiplexer_1 (
    .sel(ALU_B_MUX), .in_0(MEM_IN), .in_1(ImmI), .in_2(ImmS), .in_3(ImmB), .in_4(ImmU), .in_5(ImmJ),
    .in_6(Const1), .in_7(1'b0), .out(ALU_B));
  ALU_shift_step alu_shift_step_1 (
    .CLK(CLK), .nCLK(nCLK), .nRESET(nALU_RESET), .nEN(nSTEPDONE), .LOADLEN_SH(alu_shift_step_1_loadlen_sh),
    .nOUTPUT_SH(alu_shift_step_1_noutput_sh), .RESET_SH(alu_shift_step_1_reset_sh));
  ALU alu_1 (
    .CLK(BUS_CLK), .A(ALU_A), .B(ALU_B), .N(ALU_N), .nRESET_ALU(nALU_RESET), .CLK_F(ALU_FLAG_LATCH),
    .S(ALU_OP), .LOADLEN_SH(alu_shift_step_1_loadlen_sh), .nOUTPUT_SH(alu_shift_step_1_noutput_sh),
    .RESET_SH(alu_shift_step_1_reset_sh));  // open: FLAG, OUT, DLEN, DSUM
  Multiplexer #(.Selector_Bits(2)) multiplexer_2 (
    .sel(ALU_A_MUX), .in_0(RS1), .in_1(PC_OUT), .in_2(Const31), .in_3(1'b0), .out(ALU_A));
  Multiplexer multiplexer_3 (.sel(in_12), .in_0(ADDR_IN), .in_1(MEPC_OUT), .out(PC_IN));
  and and_2 (and_2_out, nRESET, nOPDONE);
  Multiplexer #(.Selector_Bits(2)) multiplexer_4 (
    .sel(REG_IN_MUX), .in_0(ADDR_IN), .in_1(MEM_OUT), .in_2(MEPC_OUT), .in_3(PC_OUT), .out(REG_IN));
  Multiplexer multiplexer_5 (.sel(OP_IN_MUX), .in_0(MEM_OUT), .in_1(IRQ_OP), .out(OP_IN));
  D_FF d_ff_2 (.D(nADDR_PE), .C(CLK), .Q(d_ff_2_q));  // open: nQ
  D_FF_AS d_ff_as_1 (.Set(~1'b1), .D(1'b1), .C(ADDR_LATCH), .Clr(~and_2_out), .Q(IRQ_OP_SnP));  // open: nQ
  // NAnd nand_2 has open pins: In_1=nMEM_OE, In_2=d_ff_2_q, out=open
  DebugShift32 debugshift32_16 (.CLK(BUS_CLK), .D(ALU_A), .nEN(1'b0), .Val(out_16));
  DebugShift32 debugshift32_17 (.CLK(BUS_CLK), .D(ALU_B), .nEN(1'b0), .Val(out_18));
  DebugShift32 debugshift32_18 (.CLK(BUS_CLK), .D(ADDR_IN), .nEN(1'b0), .Val(out_19));
  EEPROM #(.AddrBits(16), .Bits(8)) Firmware (.A(ROM_ADDR), .CS(ROM_SEL), .WE(~nMEM_WE), .OE(~nMEM_OE), .D(ROM_DATA));
  ROM #(.AddrBits(16), .isProgramMemory("true"), .Bits(32)) MicroCode (
    .A(out_13), .sel(1'b1),
    .D({MicroCode_d[31], REG_IN_MUX, ALU_B_MUX, ALU_A_MUX, MicroCode_d[23:22], OP_LATCH, nMEM_WE, nMEM_OE, nADDR_PE, ADDR_CLK, ADDR_LATCH, MicroCode_d[15:12], PC_OUT_SnP, PC_IN_LATCH, nREG_IN_EN, LASTSTEP, LEN, ALU_OP, ALU_FLAG_LATCH, nALU_RESET, ALU_N}));
  assign ROM_DATA = ~nMEM_WE ? out_38 : 8'bz;  // DriverInvSel driverinvsel_1
  Multiplexer multiplexer_6 (.sel(out_13[12]), .in_0(RS1), .in_1(ImmCSR), .out(multiplexer_6_out));
  CSR csr_1 (
    .CLK(BUS_CLK), .INA(multiplexer_6_out), .INB(in_25), .CSR_FUNC(out_13[11:10]), .ADDR_IN(ImmI),
    .ADDR_LATCH(in_24), .nRESET(nRESET), .NEW_VAL(CSR_OUT), .ADDR(CSR_Address));
  or or_1 (BUS_EN, LEN[0], LEN[1]);
  not not_2 (nPC_CNT_PE, PC_IN_LATCH);

  assign Step = out_13[4:0];

  // Other names for the same wires on the sheet: PC_OUT_LATCH = LASTSTEP; PC_CNT_EN = OP_LATCH; ALU_OUT = ADDR_IN;
  //   CSR_ADDR_LATCH = in_24; CSR_IN = in_25; FLAG = out_13[14]; FUNC3[2:0] = out_13[12:10]; IMM_SnP = BUS_EN;
  //   Mem_Dout[7:0] = Dout; Mem_Dval[7:0] = Dval; OPCODE[4:0] = out_13[9:5]; PC_IN_MUX = in_12; ROM_DIN[7:0] = out_38;
  //   RS2 = MEM_IN; SA = out_13[13]; SYS = out_13[15]

  // Notes on the sheet:
  //   CLK_RAW: Hz: 5000
  //   contents of Firmware (hex, n*v repeats v):
  //   93,0,10,0,13,1,0,0,33,97,20,0,93,3,10,0,93,1,20,0,63,1e,77,52,93,0,10,0,13,1,10,0,
  //   33,97,20,0,93,3,20,0,93,1,30,0,63,12,77,52,93,0,10,0,13,1,70,0,33,97,20,0,93,3,0,
  //   8,93,1,40,0,63,16,77,50,93,0,10,0,13,1,e0,0,33,97,20,0,b7,43,0,0,93,1,50,0,63,1a,
  //   77,4e,93,0,10,0,13,1,f0,1,33,97,20,0,b7,3,0,80,93,1,60,0,63,1e,77,4c,93,0,f0,ff,13,
  //   1,0,0,33,97,20,0,93,3,f0,ff,93,1,70,0,63,12,77,4c,93,0,f0,ff,13,1,10,0,33,97,20,0,
  //   93,3,e0,ff,93,1,80,0,63,16,77,4a,93,0,f0,ff,13,1,70,0,33,97,20,0,93,3,0,f8,93,1,90,
  //   0,63,1a,77,48,93,0,f0,ff,13,1,e0,0,33,97,20,0,b7,c3,ff,ff,93,1,a0,0,63,1e,77,46,93,
  //   0,f0,ff,13,1,f0,1,33,97,20,0,b7,3,0,80,93,1,b0,0,63,12,77,46,b7,20,21,21,93,80,10,
  //   12,13,1,0,0,33,97,20,0,b7,23,21,21,93,83,13,12,93,1,c0,0,63,12,77,44,b7,20,21,21,
  //   93,80,10,12,13,1,10,0,33,97,20,0,b7,43,42,42,93,83,23,24,93,1,d0,0,63,12,77,42,b7,
  //   20,21,21,93,80,10,12,13,1,70,0,33,97,20,0,b7,93,90,90,93,83,3,8,93,1,e0,0,63,12,77,
  //   40,b7,20,21,21,93,80,10,12,13,1,e0,0,33,97,20,0,b7,43,48,48,93,1,f0,0,63,14,77,3e,
  //   b7,20,21,21,93,80,10,12,13,1,f0,1,33,97,20,0,b7,3,0,80,93,1,0,1,63,16,77,3c,b7,20,
  //   21,21,93,80,10,12,13,1,0,fc,33,97,20,0,b7,23,21,21,93,83,13,12,93,1,10,1,63,16,77,
  //   3a,b7,20,21,21,93,80,10,12,13,1,10,fc,33,97,20,0,b7,43,42,42,93,83,23,24,93,1,20,
  //   1,63,16,77,38,b7,20,21,21,93,80,10,12,13,1,70,fc,33,97,20,0,b7,93,90,90,93,83,3,8,
  //   93,1,30,1,63,16,77,36,b7,20,21,21,93,80,10,12,13,1,e0,fc,33,97,20,0,b7,43,48,48,93,
  //   1,40,1,63,18,77,34,93,0,10,0,13,1,70,0,b3,90,20,0,93,3,0,8,93,1,60,1,63,9c,70,32,
  //   93,0,10,0,13,1,e0,0,33,91,20,0,b7,43,0,0,93,1,70,1,63,10,71,32,93,0,30,0,b3,90,10,
  //   0,93,3,80,1,93,1,80,1,63,96,70,30,13,2,0,0,93,0,10,0,13,1,70,0,33,97,20,0,13,3,7,
  //   0,13,2,12,0,93,2,20,0,e3,14,52,fe,93,3,0,8,93,1,90,1,63,10,73,2e,13,2,0,0,93,0,10,
  //   0,13,1,e0,0,33,97,20,0,13,0,0,0,13,3,7,0,13,2,12,0,93,2,20,0,e3,12,52,fe,b7,43,0,
  //   0,93,1,a0,1,63,18,73,2a,13,2,0,0,93,0,10,0,13,1,f0,1,33,97,20,0,13,0,0,0,13,0,0,0,
  //   13,3,7,0,13,2,12,0,93,2,20,0,e3,10,52,fe,b7,3,0,80,93,1,b0,1,63,1e,73,26,13,2,0,0,
  //   93,0,10,0,13,1,70,0,33,97,20,0,13,2,12,0,93,2,20,0,e3,16,52,fe,93,3,0,8,93,1,c0,1,
  //   63,1a,77,24,13,2,0,0,93,0,10,0,13,1,e0,0,13,0,0,0,33,97,20,0,13,2,12,0,93,2,20,0,
  //   e3,14,52,fe,b7,43,0,0,93,1,d0,1,63,14,77,22,13,2,0,0,93,0,10,0,13,1,f0,1,13,0,0,0,
  //   13,0,0,0,33,97,20,0,13,2,12,0,93,2,20,0,e3,12,52,fe,b7,3,0,80,93,1,e0,1,63,1c,77,
  //   1e,13,2,0,0,93,0,10,0,13,0,0,0,13,1,70,0,33,97,20,0,13,2,12,0,93,2,20,0,e3,14,52,
  //   fe,93,3,0,8,93,1,f0,1,63,16,77,1c,13,2,0,0,93,0,10,0,13,0,0,0,13,1,e0,0,13,0,0,0,
  //   33,97,20,0,13,2,12,0,93,2,20,0,e3,12,52,fe,b7,43,0,0,93,1,0,2,63,1e,77,18,13,2,0,
  //   0,93,0,10,0,13,0,0,0,13,0,0,0,13,1,f0,1,33,97,20,0,13,2,12,0,93,2,20,0,e3,12,52,fe,
  //   b7,3,0,80,93,1,10,2,63,16,77,16,13,2,0,0,13,1,70,0,93,0,10,0,33,97,20,0,13,2,12,0,
  //   93,2,20,0,e3,16,52,fe,93,3,0,8,93,1,20,2,63,12,77,14,13,2,0,0,13,1,e0,0,93,0,10,0,
  //   13,0,0,0,33,97,20,0,13,2,12,0,93,2,20,0,e3,14,52,fe,b7,43,0,0,93,1,30,2,63,1c,77,
  //   10,13,2,0,0,13,1,f0,1,93,0,10,0,13,0,0,0,13,0,0,0,33,97,20,0,13,2,12,0,93,2,20,0,
  //   e3,12,52,fe,b7,3,0,80,93,1,40,2,63,14,77,e,13,2,0,0,13,1,70,0,13,0,0,0,93,0,10,0,
  //   33,97,20,0,13,2,12,0,93,2,20,0,e3,14,52,fe,93,3,0,8,93,1,50,2,63,1e,77,a,13,2,0,0,
  //   13,1,e0,0,13,0,0,0,93,0,10,0,13,0,0,0,33,97,20,0,13,2,12,0,93,2,20,0,e3,12,52,fe,
  //   b7,43,0,0,93,1,60,2,63,16,77,8,13,2,0,0,13,1,f0,1,13,0,0,0,13,0,0,0,93,0,10,0,33,
  //   97,20,0,13,2,12,0,93,2,20,0,e3,12,52,fe,b7,3,0,80,93,1,70,2,63,1e,77,4,93,0,f0,0,
  //   33,11,10,0,93,3,0,0,93,1,80,2,63,14,71,4,93,0,0,2,33,91,0,0,93,3,0,2,93,1,90,2,63,
  //   1a,71,2,b3,10,0,0,93,3,0,0,93,1,a0,2,63,92,70,2,93,0,0,40,37,11,0,0,13,1,1,80,33,
  //   90,20,0,93,3,0,0,93,1,b0,2,63,14,70,0,63,10,30,2,63,80,1,0,13,85,1,0,93,91,11,0,93,
  //   e1,11,0,93,8,d0,5,6f,0,0,0,73,0,0,0,93,1,10,0,93,8,d0,5,13,5,0,0,6f,0,0,0,73,0,0,
  //   0,73,10,0,c0
  //   contents of MicroCode (hex, n*v repeats v):
  //   1d1c0a8a,190202,130202,1d0242,170202,1d0242,170202,1d0242,170202,1d0242,3d0202,1d0200,
  //   41c0282,190202,130202,201d0042,201d0042,201d0042,201d0042,201d0102,0,0,0,0,0,0,0,
  //   0,0,0,0,0,1d1c0a8a,190202,130202,1d0242,170202,1d0242,170202,1d0242,170202,1d0242,
  //   3d0202,3d0202,3d0202,3d0302,0,0,0,0,0,0,0,0,0,0,0,0,0,0,0,0,0,0,1d1c0a8a,190202,130202,
  //   1d0242,170202,1d0242,170202,1d0242,170202,1d0242,3d0202,3d0202,3d0202,3d0302,0,0,
  //   0,0,0,0,0,0,0,0,0,0,0,0,0,0,0,0,1d1c0a8a,190202,130202,1d0242,170202,1d0242,170202,
  //   1d0242,170202,1d0242,3d0202,3d0202,3d0202,3d0302,0,0,0,0,0,0,0,0,0,0,0,0,0,0,0,0,
  //   0,0,1d1c0a8a,190202,130202,1d0242,170202,1d0242,170202,1d0242,170202,1d0242,3d0202,
  //   1d0200,41d0082,1d0302,0,0,0,0,0,0,0,0,0,0,0,0,0,0,0,0,0,0,1d1c0a8a,190202,130202,
  //   1d0242,170202,1d0242,170202,1d0242,170202,1d0242,3d0202,1d0200,111d0882,1d0302,0,
  //   0,0,0,0,0,0,0,0,0,0,0,0,0,0,0,0,0,1d1c0a8a,190202,130202,1d0242,170202,1d0242,170202,
  //   1d0242,170202,1d0242,3d0202,3d0202,3d0202,3d0302,0,0,0,0,0,0,0,0,0,0,0,0,0,0,0,0,
  //   0,0,1d1c0a8a,190202,130202,1d0242,170202,1d0242,170202,1d0242,170202,1d0242,3d0202,
  //   3d0202,3d0202,3d0302,0,0,0,0,0,0,0,0,0,0,0,0,0,0,0,0,0,0,1d1c0a8a,190202,130202,1d0242,
  //   170202,1d0242,170202,1d0242,170202,1d0242,3d0202,1d0200,81c0282,190202,1a0242,c0202,
  //   1c0302,0,0,0,0,0,0,0,0,0,0,0,0,0,0,0,1d1c0a8a,190202,130202,1d0242,170202,1d0242,
  //   170202,1d0242,170202,1d0242,3d0202,3d0202,3d0202,3d0302,0,0,0,0,0,0,0,0,0,0,0,0,0,
  //   0,0,0,0,0,1d1c0a8a,190202,130202,1d0242,170202,1d0242,170202,1d0242,170202,1d0242,
  //   3d0202,3d0202,3d0202,3d0302,0,0,0,0,0,0,0,0,0,0,0,0,0,0,0,0,0,0,1d1c0a8a,190202,130202,
  //   1d0242,170202,1d0242,170202,1d0242,170202,1d0242,3d0202,3d0202,3d0202,3d0302,0,0,
  //   0,0,0,0,0,0,0,0,0,0,0,0,0,0,0,0,1d1c0a8a,190202,130202,1d0242,170202,1d0242,170202,
  //   1d0242,170202,1d0242,3d0202,1d0200,1d0082,1d0302,0,0,0,0,0,0,0,0,0,0,0,0,0,0,0,0,
  //   0,0,1d1c0a8a,190202,130202,1d0242,170202,1d0242,170202,1d0242,170202,1d0242,3d0202,
  //   1d0200,131d0082,1d0302,0,0,0,0,0,0,0,0,0,0,0,0,0,0,0,0,0,0,1d1c0a8a,190202,130202,
  //   1d0242,170202,1d0242,170202,1d0242,170202,1d0242,3d0202,3d0202,3d0202,3d0302,0,0,
  //   0,0,0,0,0,0,0,0,0,0,0,0,0,0,0,0,1d1c0a8a,190202,130202,1d0242,170202,1d0242,170202,
  //   1d0242,170202,1d0242,3d0202,3d0202,3d0202,3d0302,0,0,0,0,0,0,0,0,0,0,0,0,0,0,0,0,
  //   0,0,1d1c0a8a,190202,130202,1d0242,170202,1d0242,170202,1d0242,170202,1d0242,3d0202,
  //   3d0202,3d0202,3d0302,0,0,0,0,0,0,0,0,0,0,0,0,0,0,0,0,0,0,1d1c0a8a,190202,130202,1d0242,
  //   170202,1d0242,170202,1d0242,170202,1d0242,3d0202,3d0202,3d0202,3d0302,0,0,0,0,0,0,
  //   0,0,0,0,0,0,0,0,0,0,0,0,1d1c0a8a,190202,130202,1d0242,170202,1d0242,170202,1d0242,
  //   170202,1d0242,3d0202,3d0202,3d0202,3d0302,0,0,0,0,0,0,0,0,0,0,0,0,0,0,0,0,0,0,1d1c0a8a,
  //   190202,130202,1d0242,170202,1d0242,170202,1d0242,170202,1d0242,3d0202,3d0202,3d0202,
  //   3d0302,0,0,0,0,0,0,0,0,0,0,0,0,0,0,0,0,0,0,1d1c0a8a,190202,130202,1d0242,170202,1d0242,
  //   170202,1d0242,170202,1d0242,3d0202,3d0202,3d0202,3d0302,0,0,0,0,0,0,0,0,0,0,0,0,0,
  //   0,0,0,0,0,1d1c0a8a,190202,130202,1d0242,170202,1d0242,170202,1d0242,170202,1d0242,
  //   3d0202,3d0202,3d0202,3d0302,0,0,0,0,0,0,0,0,0,0,0,0,0,0,0,0,0,0,1d1c0a8a,190202,130202,
  //   1d0242,170202,1d0242,170202,1d0242,170202,1d0242,3d0202,3d0202,3d0202,3d0302,0,0,
  //   0,0,0,0,0,0,0,0,0,0,0,0,0,0,0,0,1d1c0a8a,190202,130202,1d0242,170202,1d0242,170202,
  //   1d0242,170202,1d0242,3d0202,3d0202,3d0202,3d0302,0,0,0,0,0,0,0,0,0,0,0,0,0,0,0,0,
  //   0,0,1d1c0a8a,190202,130202,1d0242,170202,1d0242,170202,1d0242,170202,1d0242,3d0202,
  //   1d0201,1d0293,1d0206,1d0302,0,0,0,0,0,0,0,0,0,0,0,0,0,0,0,0,0,1d1c0a8a,190202,130202,
  //   1d0242,170202,1d0242,170202,1d0242,170202,1d0242,3d0202,1d0200,41d0282,1d0600,1d1d08c2,
  //   1d1d0202,191d08c2,191d08c2,191d08c2,191d0842,191d0842,191d0842,1d0302,0,0,0,0,0,0,
  //   0,0,0,1d1c0a8a,190202,130202,1d0242,170202,1d0242,170202,1d0242,170202,1d0242,3d0202,
  //   3d0202,3d0202,3d0302,0,0,0,0,0,0,0,0,0,0,0,0,0,0,0,0,0,0,1d1c0a8a,190202,130202,1d0242,
  //   170202,1d0242,170202,1d0242,170202,1d0242,3d0202,1d0200,151d0a82,1d0600,1d1d08c2,
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endmodule
